// Logisim project FINAL_CEP.circ as structural Verilog: 7 circuits, main circuit main
module main (
  input  RESET_COUNTER,
  input  X
);

  wire CLK_out, counter_display_1_a, counter_display_1_b, counter_display_1_c, counter_display_1_d,
       counter_display_1_e, counter_display_1_f, counter_display_1_g, fsm_main_1_q0_out, fsm_main_1_q1_out,
       fsm_main_1_y, RESET_out, state_display_1_a, state_display_1_b, state_display_1_c, state_display_1_d,
       state_display_1_e, state_display_1_f, state_display_1_g;

  Clock CLK (.out(CLK_out));
  Button RESET (.out(RESET_out));
  FSM_main fsm_main_1 (
    .X(X), .CLK(CLK_out), .RESET(RESET_out), .Y(fsm_main_1_y), .Q1_out(fsm_main_1_q1_out),
    .Q0_out(fsm_main_1_q0_out));
  LED Y (.in(fsm_main_1_y));
  State_Display state_display_1 (
    .Q1(fsm_main_1_q1_out), .Q0(fsm_main_1_q0_out), .a(state_display_1_a), .b(state_display_1_b),
    .c(state_display_1_c), .d(state_display_1_d), .e(state_display_1_e), .f(state_display_1_f),
    .g(state_display_1_g));
  Counter_Display counter_display_1 (
    .Y(fsm_main_1_y), .RESET_COUNT(RESET_COUNTER), .CLK(CLK_out), .a(counter_display_1_a),
    .b(counter_display_1_b), .c(counter_display_1_c), .d(counter_display_1_d), .e(counter_display_1_e),
    .f(counter_display_1_f), .g(counter_display_1_g));
  _7_Segment_Display State (
    .g(state_display_1_g), .f(state_display_1_f), .a(state_display_1_a), .b(state_display_1_b),
    .e(state_display_1_e), .d(state_display_1_d), .c(state_display_1_c));  // open: dp
  _7_Segment_Display u_7_segment_display_1 (
    .g(counter_display_1_g), .f(counter_display_1_f), .a(counter_display_1_a), .b(counter_display_1_b),
    .e(counter_display_1_e), .d(counter_display_1_d), .c(counter_display_1_c));  // open: dp

  // Notes on the sheet:
  //   Sample Input Stream (X)   0 0 1 0 0 1 1 0 0 1 0 1 0
  //   Output (Y)   0 0 1 1 0 1 0 0 0 1 1 0 1
  //   Current State (S)   1 2 3 1 2 3 0 1 2 3 1 3 1
endmodule

module D1_Logic (
  input  Q1,
  input  Q0,
  output D1
);

  // _7486 7486_1: pin names not known; wires that end beside it: 1'b1, Q0, Q1, D1, 1'b0
endmodule

module D0_logic (
  input  X,
  input  Q1,
  input  Q0,
  output D0
);

  wire n7486_1_p4;

  // _7486 7486_1: pin names not known; wires that end beside it: 1'b1, Q0, Q1, n7486_1_p4, 1'b0
  // _747266 747266_1: pin names not known; wires that end beside it: 1'b1, n7486_1_p4, X, D0, 1'b0
endmodule

module Y_Logic (
  input  X,
  input  Q1,
  input  Q0,
  output Y
);

  wire n7486_1_p4;

  // _7486 7486_1: pin names not known; wires that end beside it: 1'b1, Q0, X, n7486_1_p4, 1'b0
  // _7408 7408_1: pin names not known; wires that end beside it: 1'b1, n7486_1_p4, Q1, Y, 1'b0
endmodule

module FSM_main (
  input  X,
  input  CLK,
  input  RESET,
  output Y,
  output Q1_out,
  output Q0_out
);

  wire n7474_1_pin2, n7474_1_pin12, not_1_out;

  not not_1 (not_1_out, RESET);
  _7474 u_7474_1 (
    .pin1(not_1_out), .pin2(n7474_1_pin2), .pin3(CLK), .pin5(Q1_out), .pin13(not_1_out),
    .pin12(n7474_1_pin12), .pin11(CLK), .pin9(Q0_out));  // open: pin4, pin6, pin10, pin8
  D1_Logic d1_logic_1 (.Q1(Q1_out), .Q0(Q0_out), .D1(n7474_1_pin2));
  D0_logic d0_logic_1 (.X(X), .Q1(Q1_out), .Q0(Q0_out), .D0(n7474_1_pin12));
  Y_Logic y_logic_1 (.X(X), .Q1(Q1_out), .Q0(Q0_out), .Y(Y));
endmodule

module State_Display (
  input  Q1,
  input  Q0,
  output a,
  output b,
  output c,
  output d,
  output e,
  output f,
  output g
);

  wire n7447_1_pin2, n7447_1_pin3, n7447_1_pin9, n7447_1_pin10, n7447_1_pin11, n7447_1_pin12, n7447_1_pin13,
       n7447_1_pin14, n7447_1_pin15;

  _7447 u_7447_1 (
    .pin1(Q1), .pin2(n7447_1_pin2), .pin3(n7447_1_pin3), .pin4(n7447_1_pin3), .pin5(n7447_1_pin3),
    .pin6(n7447_1_pin2), .pin7(Q0), .pin15(n7447_1_pin15), .pin14(n7447_1_pin14), .pin13(n7447_1_pin13),
    .pin12(n7447_1_pin12), .pin11(n7447_1_pin11), .pin10(n7447_1_pin10), .pin9(n7447_1_pin9));
  _7404 u_7404_1 (
    .pin1(n7447_1_pin13), .pin2(a), .pin3(n7447_1_pin12), .pin4(b), .pin5(n7447_1_pin11), .pin6(c),
    .pin13(n7447_1_pin10), .pin12(d));  // open: pin11, pin10, pin9, pin8
  _7404 u_7404_2 (
    .pin1(n7447_1_pin9), .pin2(e), .pin3(n7447_1_pin15), .pin4(f), .pin13(n7447_1_pin14), .pin12(g));  // open: pin5, pin6, pin11, pin10, pin9, pin8
  // also tied to GND on the sheet: n7447_1_pin2
  // also tied to VCC on the sheet: n7447_1_pin3
endmodule

module Counter_Display (
  input  Y,
  input  RESET_COUNT,
  input  CLK,
  output a,
  output b,
  output c,
  output d,
  output e,
  output f,
  output g
);

  wire n7447_1_pin3, n7447_1_pin9, n7447_1_pin10, n7447_1_pin11, n7447_1_pin12, n7447_1_pin13, n7447_1_pin14,
       n7447_1_pin15, n74163_1_pin1, n74163_1_pin3, n74163_1_pin7, n74163_1_pin9, n74163_1_pin11,
       n74163_1_pin12, n74163_1_pin13, n74163_1_pin14;

  _74163 u_74163_1 (
    .pin1(n74163_1_pin1), .pin2(CLK), .pin3(n74163_1_pin3), .pin4(n74163_1_pin3), .pin5(n74163_1_pin3),
    .pin6(n74163_1_pin3), .pin7(n74163_1_pin7), .pin14(n74163_1_pin14), .pin13(n74163_1_pin13),
    .pin12(n74163_1_pin12), .pin11(n74163_1_pin11), .pin10(Y), .pin9(n74163_1_pin9));  // open: pin15
  not not_1 (n74163_1_pin1, RESET_COUNT);
  // _7400 7400_1: pin names not known; wires that end beside it: 1'b1, n74163_1_pin14, n74163_1_pin11, n74163_1_pin9, 1'b0
  _7447 u_7447_1 (
    .pin1(n74163_1_pin13), .pin2(n74163_1_pin12), .pin3(n7447_1_pin3), .pin4(n7447_1_pin3),
    .pin5(n7447_1_pin3), .pin6(n74163_1_pin11), .pin7(n74163_1_pin14), .pin15(n7447_1_pin15),
    .pin14(n7447_1_pin14), .pin13(n7447_1_pin13), .pin12(n7447_1_pin12), .pin11(n7447_1_pin11),
    .pin10(n7447_1_pin10), .pin9(n7447_1_pin9));
  _7404 u_7404_1 (
    .pin1(n7447_1_pin13), .pin2(a), .pin3(n7447_1_pin12), .pin4(b), .pin5(n7447_1_pin11), .pin6(c),
    .pin13(n7447_1_pin10), .pin12(d));  // open: pin11, pin10, pin9, pin8
  _7404 u_7404_2 (
    .pin1(n7447_1_pin9), .pin2(e), .pin3(n7447_1_pin15), .pin4(f), .pin13(n7447_1_pin14), .pin12(g));  // open: pin5, pin6, pin11, pin10, pin9, pin8
  // also tied to GND on the sheet: n74163_1_pin3
  // also tied to VCC on the sheet: {n74163_1_pin7, n7447_1_pin3}
endmodule
